# Fritzing sketch drv8825_arduino (saved by Fritzing 0.9.3b)
circuit board: 8.46667cm x 5.64444cm

parts:
  Driver_Z = DRV 8825 Stepper Motor Carrier, High Current [part_number="DRV 8825"]
  Driver_X = DRV 8825 Stepper Motor Carrier, High Current [part_number="DRV 8825"]
  Part1 = Arduino Ethernet Shield (Rev3)  # not connected
  Driver_Y = DRV 8825 Stepper Motor Carrier, High Current [part_number="DRV 8825"]
  Power_5V = Power plug
  Motor_X = polarizedheader 4pin 0.156in [package=THT]
  Motor_Z = polarizedheader 4pin 0.156in [package=THT]
  Motor_Y = polarizedheader 4pin 0.156in [package=THT]
  Y = female pin header, 2 pins [form="♀ (female)"]
  EN = female pin header, 2 pins [form="♀ (female)"]
  Z = female pin header, 2 pins [form="♀ (female)"]
  X = female pin header, 2 pins [form="♀ (female)"]
  Y_24V = Screw terminal - 2 pins [package=THT]
  Z_24V = Screw terminal - 2 pins [package=THT]
  X_24V = Screw terminal - 2 pins [package=THT]

nets:
  N1: Driver_Z.ENABLE, Driver_X.ENABLE, Driver_Y.ENABLE, EN.pin2
  N2: Driver_Z.RESET, Driver_Z.SLEEP
  N3: Driver_Z.STEP, Z.pin2
  N4: Driver_Z.DIRECTION, Z.pin1
  N5: Driver_Z.VOLTAGE_ST/_MT, Z_24V.pin1
  N6: Driver_Z.GROUND_ST/_MT, Z_24V.pin2
  N7: Driver_Z.OUT_2B, Motor_Z.pin1
  N8: Driver_Z.OUT_2A, Motor_Z.pin2
  N9: Driver_Z.OUT_1A, Motor_Z.pin3
  N10: Driver_Z.OUT_1B, Motor_Z.pin4
  N11: Driver_Z.VOLTAGE_DD, Driver_X.VOLTAGE_DD, Driver_Y.VOLTAGE_DD, Power_5V.VCC
  N12: Driver_Z.GROUND_LOG, Driver_X.GROUND_LOG, Driver_Y.GROUND_LOG, Power_5V.GND
  N13: Driver_X.RESET, Driver_X.SLEEP
  N14: Driver_X.STEP, X.pin2
  N15: Driver_X.DIRECTION, X.pin1
  N16: Driver_X.VOLTAGE_ST/_MT, X_24V.pin1
  N17: Driver_X.GROUND_ST/_MT, X_24V.pin2
  N18: Driver_X.OUT_2B, Motor_X.pin1
  N19: Driver_X.OUT_2A, Motor_X.pin2
  N20: Driver_X.OUT_1A, Motor_X.pin3
  N21: Driver_X.OUT_1B, Motor_X.pin4
  N22: Driver_Y.RESET, Driver_Y.SLEEP
  N23: Driver_Y.STEP, Y.pin2
  N24: Driver_Y.DIRECTION, Y.pin1
  N25: Driver_Y.VOLTAGE_ST/_MT, Y_24V.pin1
  N26: Driver_Y.GROUND_ST/_MT, Y_24V.pin2
  N27: Driver_Y.OUT_2B, Motor_Y.pin4
  N28: Driver_Y.OUT_2A, Motor_Y.pin3
  N29: Driver_Y.OUT_1A, Motor_Y.pin2
  N30: Driver_Y.OUT_1B, Motor_Y.pin1
