# Fritzing sketch drv8825_arduino_1.1 (saved by Fritzing 0.9.3b)
circuit board: 8.46667cm x 5.64444cm
breadboards: 1

parts:
  Power_plug1 = Power plug
  M1 = Stepper Motor - Bipolar
  M2 = Stepper Motor - Bipolar
  DRV_1 = DRV 8825 Stepper Motor Carrier, High Current [part_number="DRV 8825"]
  DRV_2 = DRV 8825 Stepper Motor Carrier, High Current [part_number="DRV 8825"]
  M3 = Stepper Motor - Bipolar
  DRV_3 = DRV 8825 Stepper Motor Carrier, High Current [part_number="DRV 8825"]
  Part1 = Arduino Ethernet Shield (Rev3)
  H1 = polarizedheader 4pin 0.156in [package=THT]  # not connected
  H2 = polarizedheader 4pin 0.156in [package=THT]  # not connected
  H3 = polarizedheader 4pin 0.156in [package=THT]  # not connected

nets:
  N1: Power_plug1.GND, DRV_1.GROUND_ST/_MT, DRV_2.GROUND_ST/_MT, DRV_3.GROUND_ST/_MT
  N2: Power_plug1.VCC, DRV_1.VOLTAGE_ST/_MT, DRV_2.VOLTAGE_ST/_MT, DRV_3.VOLTAGE_ST/_MT
  N3: M1.A, DRV_1.OUT_2B
  N4: M1.C, DRV_1.OUT_2A
  N5: M1.B, DRV_1.OUT_1A
  N6: M1.D, DRV_1.OUT_1B
  N7: M2.A, DRV_2.OUT_2B
  N8: M2.C, DRV_2.OUT_2A
  N9: M2.B, DRV_2.OUT_1A
  N10: M2.D, DRV_2.OUT_1B
  N11: DRV_1.ENABLE, DRV_3.ENABLE, Part1.D8
  N12: DRV_1.RESET, DRV_1.SLEEP, DRV_1.VOLTAGE_DD, DRV_2.RESET, DRV_2.SLEEP, DRV_2.VOLTAGE_DD, DRV_3.RESET, DRV_3.SLEEP, DRV_3.VOLTAGE_DD, Part1.5V
  N13: DRV_1.STEP, Part1.D2
  N14: DRV_1.DIRECTION, Part1.PWM_D5
  N15: DRV_1.GROUND_LOG, DRV_2.GROUND_LOG, DRV_3.GROUND_LOG, Part1.GND
  N16: DRV_2.STEP, Part1.PWM_D3
  N17: DRV_2.DIRECTION, Part1.PWM_D6
  N18: M3.A, DRV_3.OUT_2B
  N19: M3.C, DRV_3.OUT_2A
  N20: M3.B, DRV_3.OUT_1A
  N21: M3.D, DRV_3.OUT_1B
  N22: DRV_3.STEP, Part1.SDCS
  N23: DRV_3.DIRECTION, Part1.D7
